// Logisim project SimpleRISC.circ as structural Verilog: 8 circuits, main circuit Main Processor
module Main_Processor (
  input  [3:0] Reg__Address,
  input  in_2
);

  wire alu_1_is, alu_1_is_2, branchunit_1_isbranchtaken, Clock, control_unit_1_isbeq, control_unit_1_isbgt,
       control_unit_1_isimmediate, control_unit_1_isret, control_unit_1_isst, control_unit_1_isubranch,
       control_unit_1_iswb, set_flags_1_flags_e, set_flags_1_flags_gt;
  wire [1:0] control_unit_1_isld;
  wire [3:0] multiplexer_4_out, multiplexer_5_out, multiplexer_7_out;
  wire [12:0] control_unit_1_alu_signals;
  wire [26:0] rom_1_data;
  wire [31:0] adder_1_out, adder_2_out, adder_3_out, alu_1_alu_result, bit_extender_1_out,
       find_immediate_1_immx, memoryunit_1_ldresult, multiplexer_1_out, multiplexer_2_out, multiplexer_3_out,
       multiplexer_6_out, register_1_q, register_file_1_display_d, register_file_1_read_d1,
       register_file_1_read_d2, shifter_1_out;
  wire [31:27] rom_1_data_2;

  Register #(.width(32), .trigger("falling")) register_1 (
    .D(multiplexer_1_out), .Q(register_1_q), .clk(Clock), .clr(in_2));  // open: en
  Multiplexer #(.width(32), .enable("false")) multiplexer_1 (
    .in0(adder_1_out), .in1(multiplexer_2_out), .out(multiplexer_1_out), .sel(branchunit_1_isbranchtaken));
  Adder #(.width(32)) adder_1 (.a(32'h4), .b(register_1_q), .out(adder_1_out));  // open: cin, cout
  assign bit_extender_1_out = {{5{rom_1_data[26]}}, rom_1_data};  // Bit_Extender bit_extender_1
  Shifter #(.width(32)) shifter_1 (.in(bit_extender_1_out), .\dist (5'b00010), .out(shifter_1_out));
  ALU alu_1 (
    .A(register_file_1_read_d1), .B(multiplexer_3_out), .ALU_Signals(control_unit_1_alu_signals),
    .ALU_Result(alu_1_alu_result), .is(alu_1_is), .is_2(alu_1_is_2));
  Adder #(.width(32)) adder_2 (.a(shifter_1_out), .b(register_1_q), .out(adder_2_out));  // open: cin, cout
  Multiplexer #(.width(32), .enable("false")) multiplexer_2 (
    .in0(adder_2_out), .in1(register_file_1_read_d1), .out(multiplexer_2_out), .sel(control_unit_1_isret));
  // Probe on register_file_1_display_d
  Clock clock_1 (.out(Clock));
  ROM #(.addrWidth(24), .dataWidth(32)) rom_1 (
    .addr(register_1_q[25:2]), .data({rom_1_data_2, rom_1_data}));  // open: sel
  Find_Immediate find_immediate_1 (.IMM(rom_1_data[17:0]), .IMMX(find_immediate_1_immx));
  Multiplexer #(.width(32), .enable("false")) multiplexer_3 (
    .in0(register_file_1_read_d2), .in1(find_immediate_1_immx), .out(multiplexer_3_out),
    .sel(control_unit_1_isimmediate));
  Adder #(.width(32)) adder_3 (.a(register_1_q), .b(32'h4), .out(adder_3_out));  // open: cin, cout
  Set_Flags set_flags_1 (
    .isCMP(control_unit_1_alu_signals[0]), .isGreaterThan(alu_1_is), .isEqualTo(alu_1_is_2),
    .Flags_GT(set_flags_1_flags_gt), .Flags_E(set_flags_1_flags_e));
  Multiplexer #(.width(4), .enable("false")) multiplexer_4 (
    .in0(rom_1_data[17:14]), .in1(rom_1_data[25:22]), .out(multiplexer_4_out), .sel(control_unit_1_isst));
  Multiplexer #(.width(4), .enable("false")) multiplexer_5 (
    .in0(rom_1_data[21:18]), .in1(4'b1111), .out(multiplexer_5_out), .sel(control_unit_1_isret));
  Register_File register_file_1 (
    .IN_D(multiplexer_6_out), .WRITE_E(control_unit_1_iswb), .READ_D1(register_file_1_read_d1),
    .ReadA1(multiplexer_5_out), .READ_D2(register_file_1_read_d2), .ReadA2(multiplexer_4_out),
    .DISPLAY_D(register_file_1_display_d), .DisplayA(Reg__Address), .RESET(in_2), .WriteA(multiplexer_7_out),
    .CLOCK(Clock));
  MemoryUnit memoryunit_1 (
    .MAR(alu_1_alu_result), .MDR(register_file_1_read_d2), .ldResult(memoryunit_1_ldresult),
    .isSt(control_unit_1_isst), .Clock(Clock), .isLd(control_unit_1_isld[0]), .Reset(in_2));
  Multiplexer #(.select(2), .width(32), .enable("false")) multiplexer_6 (
    .in0(alu_1_alu_result), .in1(memoryunit_1_ldresult), .in2(adder_3_out), .out(multiplexer_6_out),
    .sel(control_unit_1_isld));  // open: in3
  Control_Unit control_unit_1 (
    .l_bit(rom_1_data[26]), .in_2(rom_1_data_2), .isImmediate(control_unit_1_isimmediate),
    .isSt(control_unit_1_isst), .isLd(control_unit_1_isld[0]), .isBeq(control_unit_1_isbeq),
    .isBgt(control_unit_1_isbgt), .isRet(control_unit_1_isret), .isWb(control_unit_1_iswb),
    .isUbranch(control_unit_1_isubranch), .isCall(control_unit_1_isld[1]),
    .ALU_Signals(control_unit_1_alu_signals));
  BranchUnit branchunit_1 (
    .isUBranch(control_unit_1_isubranch), .isBeq(control_unit_1_isbeq), .flags_E(set_flags_1_flags_gt),
    .isBgt(control_unit_1_isbgt), .flags__GT(set_flags_1_flags_e), .isBranchTaken(branchunit_1_isbranchtaken));
  Multiplexer #(.width(4), .enable("false")) multiplexer_7 (
    .in0(rom_1_data[25:22]), .in1(4'b1111), .out(multiplexer_7_out), .sel(control_unit_1_isld[1]));

  // Other names for the same wires on the sheet: Reset = in_2

  // Notes on the sheet:
  //   PC
  //   isBranchTaken
  //   pc+4
  //   branchTarget
  //   ALU Signals
  //   offset
  //   pc
  //   branchTarget
  //   B
  //   aluResult
  //   Instruction Memory
  //   isRet
  //   A
  //   contents of rom_1 (hex, n*v repeats v):
  //   4c800078 4cc000f0 10c8000 90000000
  //   imm
  //   is>
  //   is=
  //   pc
  //   immx
  //   isCmp
  //   rs2
  //   isImmediate
  //   rs1
  //   rd
  //   isSt
  //   op2
  //   aluResult
  //   32-Bit SIMPLE RISC PROCESSOR
  //   isRet
  //   op1
  //   reg. Address
  //   isWb
  //   address
  //   data
  //   register Value
  //   flag GT
  //   flag E
  //   opcode
  //   l bit
  //   isBranchTaken
  //   MAR
  //   IdResult
  //   isBeq
  //   isBgt
  //   isUBranch
  //   MDR
  //   data
  //   isLd
  //   isSt
  //   isLd
  //   isCall
  //   isCall
  //   rd
endmodule

// CONTROL UNIT
module Control_Unit (
  input  l_bit,
  input  [4:0] in_2,
  output isImmediate,
  output isSt,
  output isLd,
  output isBeq,
  output isBgt,
  output isRet,
  output isWb,
  output isUbranch,
  output isCall,
  output [12:0] ALU_Signals
);

  wire and_6_out, and_7_out, and_8_out, and_9_out, and_10_out, and_12_out, and_13_out, nand_1_out;

  nand nand_1 (nand_1_out, in_2[0], in_2[1]);
  and and_1 (isSt, in_2[0], in_2[1], in_2[2], in_2[3], ~in_2[4]);  // AND_Gate
  and and_2 (isLd, ~in_2[0], in_2[1], in_2[2], in_2[3], ~in_2[4]);  // AND_Gate
  and and_3 (isBeq, ~in_2[0], ~in_2[1], ~in_2[2], ~in_2[3], in_2[4]);  // AND_Gate
  and and_4 (isBgt, in_2[0], ~in_2[1], ~in_2[2], ~in_2[3], in_2[4]);  // AND_Gate
  and and_5 (isRet, ~in_2[0], ~in_2[1], in_2[2], ~in_2[3], in_2[4]);  // AND_Gate
  and and_6 (and_6_out, in_2[0], ~in_2[1], in_2[2], ~in_2[4]);  // AND_Gate
  and and_7 (and_7_out, in_2[0], in_2[2], in_2[3], ~in_2[4]);  // AND_Gate
  and and_8 (and_8_out, in_2[4], nand_1_out);
  and and_9 (and_9_out, in_2[1], ~in_2[2], ~in_2[3], in_2[4]);  // AND_Gate
  and and_10 (and_10_out, ~in_2[0], ~in_2[1], in_2[2], ~in_2[3], in_2[4]);  // AND_Gate
  and and_11 (isCall, in_2[0], in_2[1], ~in_2[2], ~in_2[3], in_2[4]);  // AND_Gate
  and and_12 (and_12_out, ~in_2[0], ~in_2[1], ~in_2[2], ~in_2[3], ~in_2[4]);  // AND_Gate
  and and_13 (and_13_out, in_2[1], in_2[2], in_2[3], ~in_2[4]);  // AND_Gate
  and and_14 (ALU_Signals[2], in_2[0], ~in_2[1], ~in_2[2], ~in_2[3], ~in_2[4]);  // AND_Gate
  and and_15 (ALU_Signals[0], in_2[0], ~in_2[1], in_2[2], ~in_2[3], ~in_2[4]);  // AND_Gate
  and and_16 (ALU_Signals[3], ~in_2[0], in_2[1], ~in_2[2], ~in_2[3], ~in_2[4]);  // AND_Gate
  and and_17 (ALU_Signals[4], in_2[0], in_2[1], ~in_2[2], ~in_2[3], ~in_2[4]);  // AND_Gate
  and and_18 (ALU_Signals[5], ~in_2[0], ~in_2[1], in_2[2], ~in_2[3], ~in_2[4]);  // AND_Gate
  and and_19 (ALU_Signals[7], ~in_2[0], in_2[1], ~in_2[2], in_2[3], ~in_2[4]);  // AND_Gate
  and and_20 (ALU_Signals[8], in_2[0], in_2[1], ~in_2[2], in_2[3], ~in_2[4]);  // AND_Gate
  and and_21 (ALU_Signals[9], ~in_2[0], ~in_2[1], in_2[2], in_2[3], ~in_2[4]);  // AND_Gate
  and and_22 (ALU_Signals[12], in_2[0], in_2[1], in_2[2], ~in_2[3], ~in_2[4]);  // AND_Gate
  and and_23 (ALU_Signals[11], ~in_2[0], in_2[1], in_2[2], ~in_2[3], ~in_2[4]);  // AND_Gate
  and and_24 (ALU_Signals[10], ~in_2[0], ~in_2[1], ~in_2[2], in_2[3], ~in_2[4]);  // AND_Gate
  and and_25 (ALU_Signals[6], in_2[0], ~in_2[1], ~in_2[2], in_2[3], ~in_2[4]);  // AND_Gate
  nor nor_1 (isWb, and_6_out, and_7_out, and_8_out);
  or or_1 (isUbranch, and_9_out, and_10_out);
  or or_2 (ALU_Signals[1], and_12_out, and_13_out);

  assign isImmediate = l_bit;

  // Notes on the sheet:
  //   OPCode 
  //   isSub
  //   isCmp
  //   isMul
  //   isDiv
  //   isMod
  //   isLsl
  //   isLsr
  //   isAsr
  //   isOr
  //   isAnd
  //   isNot
  //   isMov
  //   isAdd
  //   CONTROL UNIT 
endmodule

// Flags Unit
module Set_Flags (
  input  isCMP,
  input  isGreaterThan,
  input  isEqualTo,
  output Flags_GT,
  output Flags_E
);

  D_Flip_Flop d_ff_1 (.clk(isCMP), .D(isGreaterThan), .Q(Flags_GT));  // open: Qn, preset, en, reset
  D_Flip_Flop d_ff_2 (.clk(isCMP), .D(isEqualTo), .Q(Flags_E));  // open: Qn, preset, en, reset

  // Notes on the sheet:
  //   Flags Unit
endmodule

// Find Immx
module Find_Immediate (
  input  [17:0] IMM,
  output [31:0] IMMX
);

  wire [31:0] bit_extender_1_out, bit_extender_2_out, shifter_1_out;

  assign bit_extender_1_out = {{16{1'b0}}, IMM[15:0]};  // Bit_Extender bit_extender_1
  assign bit_extender_2_out = {{16{IMM[15]}}, IMM[15:0]};  // Bit_Extender bit_extender_2
  Shifter #(.width(32)) shifter_1 (.in(bit_extender_1_out), .\dist (5'b10000), .out(shifter_1_out));
  Multiplexer #(.select(2), .width(32), .enable("false")) multiplexer_1 (
    .in0(bit_extender_2_out), .in1(bit_extender_1_out), .in2(shifter_1_out), .out(IMMX), .sel(IMM[17:16]));  // open: in3

  // Notes on the sheet:
  //   Modifier Bits
  //   Calculate Immediate Value
  //   Default
  //   Unsigned
  //   High
endmodule

module ALU (
  input  [31:0] A,
  input  [31:0] B,
  input  [12:0] ALU_Signals,
  output [31:0] ALU_Result,
  output is,
  output is_2
);

  wire [31:0] adder_1_out, and_1_out, divider_1_out, divider_1_rem, multiplier_1_out, not_1_out, or_1_out,
       shifter_1_out, shifter_2_out, shifter_3_out, subtractor_1_out;

  Adder #(.width(32)) adder_1 (.a(A), .b(B), .out(adder_1_out));  // open: cin, cout
  Subtractor #(.width(32)) subtractor_1 (.a(A), .b(B), .out(subtractor_1_out));  // open: bin, bout
  Multiplier #(.width(32)) multiplier_1 (.a(A), .b(B), .out(multiplier_1_out));  // open: cin, cout
  Divider #(.width(32)) divider_1 (.a(A), .b(B), .out(divider_1_out), .rem(divider_1_rem));  // open: upper
  Comparator #(.width(32)) comparator_1 (.a(A), .b(B), .gt(is), .eq(is_2));  // open: lt
  Shifter #(.width(32)) shifter_1 (.in(A), .\dist (B[4:0]), .out(shifter_1_out));
  Shifter #(.width(32), .shift("lr")) shifter_2 (.in(A), .\dist (B[4:0]), .out(shifter_2_out));
  Shifter #(.width(32), .shift("ar")) shifter_3 (.in(A), .\dist (B[4:0]), .out(shifter_3_out));
  assign not_1_out = ~B;  // NOT_Gate not_1, 32 bits wide
  assign and_1_out = A & B;  // AND_Gate and_1, 32 bits wide
  assign or_1_out = A | B;  // OR_Gate or_1, 32 bits wide
  assign ALU_Result = ALU_Signals[1] ? adder_1_out : 32'bz;  // Controlled_Buffer controlled_buffer_1
  assign ALU_Result = ALU_Signals[2] ? subtractor_1_out : 32'bz;  // Controlled_Buffer controlled_buffer_2
  assign ALU_Result = ALU_Signals[3] ? multiplier_1_out : 32'bz;  // Controlled_Buffer controlled_buffer_3
  assign ALU_Result = ALU_Signals[4] ? divider_1_out : 32'bz;  // Controlled_Buffer controlled_buffer_4
  assign ALU_Result = ALU_Signals[5] ? divider_1_rem : 32'bz;  // Controlled_Buffer controlled_buffer_5
  assign ALU_Result = ALU_Signals[6] ? B : 32'bz;  // Controlled_Buffer controlled_buffer_6
  assign ALU_Result = ALU_Signals[7] ? shifter_1_out : 32'bz;  // Controlled_Buffer controlled_buffer_7
  assign ALU_Result = ALU_Signals[8] ? shifter_2_out : 32'bz;  // Controlled_Buffer controlled_buffer_8
  assign ALU_Result = ALU_Signals[9] ? shifter_3_out : 32'bz;  // Controlled_Buffer controlled_buffer_9
  assign ALU_Result = ALU_Signals[10] ? not_1_out : 32'bz;  // Controlled_Buffer controlled_buffer_10
  assign ALU_Result = ALU_Signals[11] ? and_1_out : 32'bz;  // Controlled_Buffer controlled_buffer_11
  assign ALU_Result = ALU_Signals[12] ? or_1_out : 32'bz;  // Controlled_Buffer controlled_buffer_12

  // Notes on the sheet:
  //   isAdd
  //   isSub
  //   isMul
  //   isDiv
  //   isCmp
  //   isLsl
  //   isLsr
  //   isAsr
  //   isNot
  //   isAnd
  //   isOr
  //   isMod
  //   ALU
endmodule

// Memory Unit
module MemoryUnit (
  input  [31:0] MAR,
  input  isLd,
  input  [31:0] MDR,
  input  isSt,
  input  Clock,
  input  Reset,
  output [31:0] ldResult
);

  RAM #(.addrWidth(24), .dataWidth(32), .bus("separate")) ram_1 (
    .addr(MAR[25:2]), .din(MDR), .data(ldResult), .str(isSt), .clk(Clock), .ld(isLd), .clr(Reset));  // open: sel

  // Notes on the sheet:
  //   Memory Unit
endmodule

// Branch Unit
module BranchUnit (
  input  isUBranch,
  input  isBeq,
  input  flags_E,
  input  isBgt,
  input  flags__GT,
  output isBranchTaken
);

  wire and_1_out, and_2_out;

  and and_1 (and_1_out, isBeq, flags_E);
  and and_2 (and_2_out, isBgt, flags__GT);
  or or_1 (isBranchTaken, isUBranch, and_1_out, and_2_out);

  // Notes on the sheet:
  //   Branch Unit
endmodule

// Register File
module Register_File (
  input  CLOCK,
  input  RESET,
  input  [3:0] ReadA1,
  input  [31:0] IN_D,
  input  WRITE_E,
  input  [3:0] WriteA,
  input  [3:0] ReadA2,
  input  [3:0] DisplayA,
  output [31:0] READ_D1,
  output [31:0] READ_D2,
  output [31:0] DISPLAY_D
);

  wire demultiplexer_1_out0, demultiplexer_1_out1, demultiplexer_1_out2, demultiplexer_1_out3,
       demultiplexer_1_out4, demultiplexer_1_out5, demultiplexer_1_out6, demultiplexer_1_out7,
       demultiplexer_1_out8, demultiplexer_1_out9, demultiplexer_1_out10, demultiplexer_1_out11,
       demultiplexer_1_out12, demultiplexer_1_out13, demultiplexer_1_out14, demultiplexer_1_out15,
       multiplexer_2_out, or_1_out, or_2_out;
  wire [31:0] multiplexer_1_out, R0_q, R1_q, R2_q, R3_q, R4_q, R5_q, R6_q, R7_q, R8_q, R9_q, R10_q, R11_q,
       R12_q, R13_q, R14_q, R15_q;

  Demultiplexer #(.select(4), .disabled(0), .enable("false")) demultiplexer_1 (
    .out0(demultiplexer_1_out0), .out1(demultiplexer_1_out1), .out2(demultiplexer_1_out2),
    .out3(demultiplexer_1_out3), .out4(demultiplexer_1_out4), .out5(demultiplexer_1_out5),
    .out6(demultiplexer_1_out6), .out7(demultiplexer_1_out7), .out8(demultiplexer_1_out8),
    .out9(demultiplexer_1_out9), .out10(demultiplexer_1_out10), .out11(demultiplexer_1_out11),
    .out12(demultiplexer_1_out12), .out13(demultiplexer_1_out13), .out14(demultiplexer_1_out14),
    .out15(demultiplexer_1_out15), .in(WRITE_E), .sel(WriteA));
  Multiplexer #(.width(32), .enable("false")) multiplexer_1 (
    .in0(IN_D), .in1(32'h3fffffc), .out(multiplexer_1_out), .sel(RESET));
  or or_1 (or_1_out, demultiplexer_1_out14, RESET);
  or or_2 (or_2_out, CLOCK, RESET);
  Multiplexer #(.enable("false")) multiplexer_2 (.in0(or_2_out), .out(multiplexer_2_out), .sel(1'b0));  // open: in1
  Register #(.width(32)) R0 (.D(IN_D), .en(demultiplexer_1_out0), .Q(R0_q), .clk(CLOCK), .clr(RESET));
  Register #(.width(32)) R1 (.D(IN_D), .en(demultiplexer_1_out1), .Q(R1_q), .clk(CLOCK), .clr(RESET));
  Register #(.width(32)) R2 (.D(IN_D), .en(demultiplexer_1_out2), .Q(R2_q), .clk(CLOCK), .clr(RESET));
  Register #(.width(32)) R3 (.D(IN_D), .en(demultiplexer_1_out3), .Q(R3_q), .clk(CLOCK), .clr(RESET));
  Register #(.width(32)) R4 (.D(IN_D), .en(demultiplexer_1_out4), .Q(R4_q), .clk(CLOCK), .clr(RESET));
  Register #(.width(32)) R5 (.D(IN_D), .en(demultiplexer_1_out5), .Q(R5_q), .clk(CLOCK), .clr(RESET));
  Register #(.width(32)) R6 (.D(IN_D), .en(demultiplexer_1_out6), .Q(R6_q), .clk(CLOCK), .clr(RESET));
  Register #(.width(32)) R7 (.D(IN_D), .en(demultiplexer_1_out7), .Q(R7_q), .clk(CLOCK), .clr(RESET));
  Register #(.width(32)) R8 (.D(IN_D), .en(demultiplexer_1_out8), .Q(R8_q), .clk(CLOCK), .clr(RESET));
  Register #(.width(32)) R9 (.D(IN_D), .en(demultiplexer_1_out9), .Q(R9_q), .clk(CLOCK), .clr(RESET));
  Register #(.width(32)) R10 (.D(IN_D), .en(demultiplexer_1_out10), .Q(R10_q), .clk(CLOCK), .clr(RESET));
  Register #(.width(32)) R11 (.D(IN_D), .en(demultiplexer_1_out11), .Q(R11_q), .clk(CLOCK), .clr(RESET));
  Register #(.width(32)) R12 (.D(IN_D), .en(demultiplexer_1_out12), .Q(R12_q), .clk(CLOCK), .clr(RESET));
  Register #(.width(32)) R13 (.D(IN_D), .en(demultiplexer_1_out13), .Q(R13_q), .clk(CLOCK), .clr(RESET));
  Register #(.width(32)) R14 (.D(multiplexer_1_out), .en(or_1_out), .Q(R14_q), .clk(multiplexer_2_out));  // open: clr
  Register #(.width(32)) R15 (.D(IN_D), .en(demultiplexer_1_out15), .Q(R15_q), .clk(CLOCK), .clr(RESET));
  Multiplexer #(.select(4), .width(32), .disabled(0), .enable("false")) multiplexer_3 (
    .in0(R0_q), .in1(R1_q), .in2(R2_q), .in3(R3_q), .in4(R4_q), .in5(R5_q), .in6(R6_q), .in7(R7_q),
    .in8(R8_q), .in9(R9_q), .in10(R10_q), .in11(R11_q), .in12(R12_q), .in13(R13_q), .in14(R14_q),
    .in15(R15_q), .out(READ_D1), .sel(ReadA1));
  Multiplexer #(.select(4), .width(32), .disabled(0), .enable("false")) multiplexer_4 (
    .in0(R0_q), .in1(R1_q), .in2(R2_q), .in3(R3_q), .in4(R4_q), .in5(R5_q), .in6(R6_q), .in7(R7_q),
    .in8(R8_q), .in9(R9_q), .in10(R10_q), .in11(R11_q), .in12(R12_q), .in13(R13_q), .in14(R14_q),
    .in15(R15_q), .out(READ_D2), .sel(ReadA2));
  Multiplexer #(.select(4), .width(32), .disabled(0), .enable("false")) multiplexer_5 (
    .in0(R0_q), .in1(R1_q), .in2(R2_q), .in3(R3_q), .in4(R4_q), .in5(R5_q), .in6(R6_q), .in7(R7_q),
    .in8(R8_q), .in9(R9_q), .in10(R10_q), .in11(R11_q), .in12(R12_q), .in13(R13_q), .in14(R14_q),
    .in15(R15_q), .out(DISPLAY_D), .sel(DisplayA));

  // Notes on the sheet:
  //   REGISTER FILE 
endmodule
